# Fritzing sketch pompe_nutiments (saved by Fritzing 0.9.3b)
breadboards: 1

parts:
  Raspberry_Pi_1 = Raspberry Pi 3 [part_number=RPI-3-V1.2]
  LED1 = LED - 5mm [color="Red (633nm)" package="5 mm [THT]"]
  S1 = Toggle Switch [package=THT]
  R1 = Resistor [tolerance=±5% resistance=220 package=THT]
  S2 = Pushbutton [package=THT]
  V1 = DC Power [voltage=6]
  U1 = Sharp PC817 [package=THT]
  R2 = Resistor [tolerance=±5% resistance=33 package=THT]
  U2 = RELAY [package=relay-t9a-2]

nets (from the schematic view):
  N1: Raspberry_Pi_1.GIPO21, R2.Pin_0
  N2: Raspberry_Pi_1.GND, R1.Pin_1, V1.V-
  N3: Raspberry_Pi_1.5V, U1.Pin_4
  N4: LED1.anode, S1.COM
  N5: S1.L1, U2.MAIN
  N6: S1.L2, S2.leg1
  N7: S2.leg0, V1.V+, U2.NO
  N8: U1.Pin_1, R2.Pin_1
  N9: U1.Pin_2, U2.COIL2
  N10: U1.Pin_3, U2.COIL1
  GND: U2.NC
